# Fritzing sketch Soldering Station (saved by Fritzing 0.9.3b)

parts:
  U2 = MOC3031-M [package=dil06]
  R1 = Resistor [tolerance=±5% resistance=470 package=THT]
  R2 = Resistor [tolerance=±5% resistance=220 package=THT]
  R3 = Resistor [tolerance=±5% resistance=220 package=THT]
  J2 = Screw terminal - 2 pins [package=THT]
  U3 = TRIAC [package=to-220]
  U4 = MOC3031-M [package=dil06]
  R4 = Resistor [tolerance=±5% resistance=470 package=THT]
  R5 = Resistor [tolerance=±5% resistance=220 package=THT]
  R6 = Resistor [tolerance=±5% resistance=220 package=THT]
  J4 = Screw terminal - 2 pins [package=THT]
  U5 = TRIAC [package=to-220]
  U6 = MAX6675 [package=so08]
  C4 = Ceramic Capacitor [capacitance=0.1µF voltage=16V package="100 mil [THT, multilayer]"]
  J5 = Screw terminal - 2 pins [package=THT]
  U7 = MAX6675 [package=so08]
  C5 = Ceramic Capacitor [capacitance=0.1µF voltage=16V package="100 mil [THT, multilayer]"]
  J6 = Screw terminal - 2 pins [package=THT]
  Rotary_Encoder_Breakout = KY-040 Rotary encoder [package="Breakout board"]
  I2C_OLED_LCD = Grove OLED 128x96
  S1 = Pushbutton [package="[THT]"]
  Reed_Switch = Reed switch [package=THT]
  BT138 = MOSFET-NCHANNEL [package=to220v]
  R7 = Resistor [tolerance=±5% resistance=220 package=THT]
  J7 = Screw terminal - 2 pins [package=THT]
  BT138_2 = MOSFET-NCHANNEL [package=to220v]
  R8 = Resistor [tolerance=±5% resistance=220 package=THT]
  J8 = Screw terminal - 2 pins [package=THT]
  L7805 = Voltage Regulator - 5V [package="TO220 [THT]"]
  C6 = Electrolytic Capacitor [capacitance=1µF package="100 mil [THT, electrolytic]"]
  C7 = Electrolytic Capacitor [capacitance=1µF package="100 mil [THT, electrolytic]"]
  J9 = Screw terminal - 2 pins [package=THT]
  Arduino_Nano = Arduino Nano (Rev3.0)
  Toggle_Switch_220V = Toggle Switch [package=THT]
  R9 = Resistor [tolerance=±5% resistance=1k package=THT]
  R10 = Resistor [tolerance=±5% resistance=1k package=THT]

nets:
  N1: U2.1, R1.Pin_1
  GND: U2.2, U4.2, U6.VSS, U6.T-, C4.0, C4.1, J5.pin2, U7.VSS, U7.T-, C5.0, C5.1, J6.pin2, Rotary_Encoder_Breakout.GND, I2C_OLED_LCD.GND, S1.Pin_1, S1.Pin_2, Reed_Switch.pin_2, BT138.S, BT138_2.S, L7805.GND, C6.-, C7.-, J9.pin2, Arduino_Nano.GND
  N2: U2.4, R3.Pin_1, U3.G
  N3: U2.6, R2.Pin_0
  D7: R1.Pin_0, R4.Pin_0, Reed_Switch.pin_1, Arduino_Nano.D7
  N4: R2.Pin_1, J2.pin1, U3.MT2
  N5: R3.Pin_0, J2.pin2, U3.MT1
  N6: U4.1, R4.Pin_1
  N7: U4.4, R6.Pin_1, U5.G
  N8: U4.6, R5.Pin_0
  N9: R5.Pin_1, J4.pin1, U5.MT2
  N10: R6.Pin_0, J4.pin2, U5.MT1
  N11: U6.T+, J5.pin1
  VCC 5V: U6.VDD, U7.VDD, Rotary_Encoder_Breakout.Vcc, I2C_OLED_LCD.VCC, L7805.output_voltage, C7.+, Arduino_Nano.5V
  D13: U6.SCK, U7.SCK, Arduino_Nano.D13/SCK
  D10: U6.CS, Arduino_Nano.D10
  D12: U6.MISO, U7.MISO, Arduino_Nano.D12/MISO
  N12: U7.T+, J6.pin1
  D8: U7.CS, Arduino_Nano.D8
  A2: Rotary_Encoder_Breakout.SW, Arduino_Nano.A2
  D3: Rotary_Encoder_Breakout.DT, Arduino_Nano.D3
  D2: Rotary_Encoder_Breakout.CLK, Arduino_Nano.D2
  A4: I2C_OLED_LCD.SDA, Arduino_Nano.A4
  A5: I2C_OLED_LCD.SCL, Arduino_Nano.A5
  RST: S1.Pin_3, S1.Pin_4, Arduino_Nano.RESET
  N13: BT138.G, R7.Pin_1, R10.Pin_0
  N14: BT138.D, J7.pin1
  D5: R7.Pin_0, Arduino_Nano.D5
  24V: J7.pin2
  N15: BT138_2.G, R8.Pin_1, R9.Pin_0
  N16: BT138_2.D, J8.pin1
  D9: R8.Pin_0, Arduino_Nano.D9
  12V: J8.pin2, L7805.input_voltage, C6.+, J9.pin1
  D6: Arduino_Nano.D6
  SW Live: Toggle_Switch_220V.L1
  Live: Toggle_Switch_220V.COM

notes:
  Cooling Fan
  MOC3021 can be substituted with
  MOC3020 or S21ME4

custom parts:
  TRIAC: Generic TRIAC, TO-220 package
  KY-040 Rotary encoder: KY-040 Rotary Encoder with switch on breakout borad from AZ Delivery
  Voltage Regulator - 5V: 5V DC Voltage Regulator
